# Fritzing sketch traffic_light_schema (saved by Fritzing 0.7.11b)
breadboards: 1

parts:
  U1 = Arduino Mega
  Arduino_Ethernet_Shield1 = Arduino Ethernet Shield  # not connected
  R6 = Resistor [tolerance=±5% resistance=220 package=THT]
  Q1 = NPN-Transistor [part_number=C547B package="TO92 [THT]"]
  Power_plug1 = Power plug
  LED2 = Glühbirnchen  # not connected
  R7 = Resistor [tolerance=±5% resistance=220 package=THT]
  Q2 = NPN-Transistor [part_number=C547B package="TO92 [THT]"]
  LED4 = Glühbirnchen  # not connected
  R8 = Resistor [tolerance=±5% resistance=220 package=THT]
  Q3 = NPN-Transistor [part_number=C547B package="TO92 [THT]"]
  LED5 = Glühbirnchen  # not connected
  R9 = Resistor [tolerance=±5% resistance=220 package=THT]
  Q4 = NPN-Transistor [part_number=C547B package="TO92 [THT]"]
  LED6 = Glühbirnchen  # not connected
  R10 = Resistor [tolerance=±5% resistance=220 package=THT]
  Q5 = NPN-Transistor [part_number=C547B package="TO92 [THT]"]
  LED7 = Glühbirnchen  # not connected
  R11 = Resistor [tolerance=±5% resistance=220 package=THT]
  Q6 = NPN-Transistor [part_number=C547B package="TO92 [THT]"]
  LED8 = Glühbirnchen  # not connected
  R12 = Resistor [tolerance=±5% resistance=220 package=THT]
  Q7 = NPN-Transistor [part_number=C547B package="TO92 [THT]"]
  LED9 = Glühbirnchen  # not connected
  R13 = Resistor [tolerance=±5% resistance=220 package=THT]
  Q8 = NPN-Transistor [part_number=C547B package="TO92 [THT]"]
  LED10 = Glühbirnchen  # not connected
  R14 = Resistor [tolerance=±5% resistance=220 package=THT]
  Q9 = NPN-Transistor [part_number=C547B package="TO92 [THT]"]
  LED11 = Glühbirnchen  # not connected
  R15 = Resistor [tolerance=±5% resistance=220 package=THT]
  Q10 = NPN-Transistor [part_number=C547B package="TO92 [THT]"]
  LED12 = Glühbirnchen  # not connected

nets:
  N1: U1.D22, R15.Pin_1
  N2: U1.D23, R6.Pin_0
  N3: U1.D24, R14.Pin_0
  N4: U1.D25, R7.Pin_0
  N5: U1.D26, R13.Pin_0
  N6: U1.D27, R8.Pin_0
  N7: U1.D28, R12.Pin_0
  N8: U1.D29, R9.Pin_0
  N9: U1.D30, R11.Pin_0
  N10: U1.D31, R10.Pin_0
  N11: R6.Pin_1, Q1.B
  N12: Q1.C, Power_plug1.GND, Q2.C, Q3.C, Q4.C, Q5.C, Q6.C, Q7.C, Q8.C, Q9.C, Q10.C
  N13: R7.Pin_1, Q2.B
  N14: R8.Pin_1, Q3.B
  N15: R9.Pin_1, Q4.B
  N16: R10.Pin_1, Q5.B
  N17: R11.Pin_1, Q6.B
  N18: R12.Pin_1, Q7.B
  N19: R13.Pin_1, Q8.B
  N20: R14.Pin_1, Q9.B
  N21: R15.Pin_0, Q10.B

notes:
  5V Netzteil
  10 Stück Glühbirnchen 5V

custom parts:
  Glühbirnchen: Glühbirnchen bis 5.0V
